// Logisim project ID_EX.circ as structural Verilog: 1 circuit, main circuit main
module main (
  input  [31:0] in_1,
  input  [31:0] in_2,
  input  [31:0] in_3,
  input  [31:0] in_4,
  input  [4:0] in_5,
  input  [4:0] in_6,
  input  CLK,
  output [31:0] out_8,
  output [31:0] out_9,
  output [31:0] out_10,
  output [31:0] out_11,
  output [4:0] out_12,
  output [4:0] out_13
);

  Register #(.width(32)) register_1 (.D(in_1), .Q(out_8), .clk(CLK));  // open: en, clr
  Register #(.width(32)) register_2 (.D(in_2), .Q(out_9), .clk(CLK));  // open: en, clr
  Register #(.width(32)) register_3 (.D(in_3), .Q(out_10), .clk(CLK));  // open: en, clr
  Register #(.width(32)) register_4 (.D(in_4), .Q(out_11), .clk(CLK));  // open: en, clr
  Register #(.width(5)) register_5 (.D(in_5), .Q(out_12), .clk(CLK));  // open: en, clr
  Register #(.width(5)) register_6 (.D(in_6), .Q(out_13), .clk(CLK));  // open: en, clr

  // Other names for the same wires on the sheet: Inst_15_0[31:0] = in_4; Inst_15_0__Out[31:0] = out_11;
  //   Inst_15_11[4:0] = in_6; Inst_15_11__Out[4:0] = out_13; Inst_20_16[4:0] = in_5; Inst_20_16__Out[4:0] = out_12;
  //   PC_4[31:0] = in_1; PC_4_Out[31:0] = out_8; Read1[31:0] = in_2; Read1_Out[31:0] = out_9; Read2[31:0] = in_3;
  //   Read2_Out[31:0] = out_10
endmodule
